# Fritzing sketch Blink (saved by Fritzing 0.7.0b)
breadboards: 1

parts:
  Arduino2 = Arduino
  Arduino3 = Arduino
  LED2 = LED - 5mm [color="Red (633nm)" package="5 mm [THT]"]
  LED3 = LED - 5mm [color="Red (633nm)" package="5 mm [THT]"]
  R1 = Resistor [tolerance=±5% resistance=220 package=THT]

nets:
  N1: Arduino2.D12, LED3.anode
  N2: Arduino2.GND, R1.Pin_1
  N3: Arduino3.aref, Arduino3.GND, Arduino3.D12, Arduino3.D11, Arduino3.D9, LED2.cathode, LED2.anode
  N4: LED3.cathode, R1.Pin_0

// code stored in the sketch: Blink.ino
/*
  Blink
  Turns on an LED on for one second, then off for one second, repeatedly.
 
  This example code is in the public domain.
 */

void setup() {                
  // initialize the digital pin as an output.
  // Pin 13 has an LED connected on most Arduino boards:
  pinMode(13, OUTPUT);     
}

void loop() {
  digitalWrite(13, HIGH);   // set the LED on
  delay(1000);              // wait for a second
  digitalWrite(13, LOW);    // set the LED off
  delay(1000);              // wait for a second
}
