# Fritzing sketch Button (saved by Fritzing 0.7.0b)
breadboards: 1

parts:
  Arduino2 = Arduino
  LED3 = LED - 5mm [color="Red (633nm)" package="5 mm [THT]"]
  S1 = Pushbutton [package="[THT]"]
  R2 = Resistor [tolerance=±5% resistance=220 package=THT]
  R3 = Resistor [resistance=10k tolerance=±5% package=THT]

nets:
  N1: Arduino2.D12, LED3.anode
  N2: Arduino2.D2, S1.Pin_1, S1.Pin_2, R3.Pin_0
  N3: Arduino2.+5V, S1.Pin_3, S1.Pin_4
  N4: Arduino2.GND, R2.Pin_1, R3.Pin_1
  N5: LED3.cathode, R2.Pin_0

// code stored in the sketch: Blink.ino
/*
  Blink
  Turns on an LED on for one second, then off for one second, repeatedly.
 
  This example code is in the public domain.
 */

void setup() {                
  // initialize the digital pin as an output.
  // Pin 13 has an LED connected on most Arduino boards:
  pinMode(13, OUTPUT);     
}

void loop() {
  digitalWrite(13, HIGH);   // set the LED on
  delay(1000);              // wait for a second
  digitalWrite(13, LOW);    // set the LED off
  delay(1000);              // wait for a second
}
