# Fritzing sketch Bargraph (Simple) (saved by Fritzing 0.7.0b)
breadboards: 1

parts:
  Arduino1 = Arduino
  LED1 = LED - 5mm [color="Red (633nm)" package="5 mm [THT]"]
  LED2 = LED - 5mm [color="Red (633nm)" package="5 mm [THT]"]
  LED3 = LED - 5mm [color="Yellow (585nm)" package="5 mm [THT]"]
  LED4 = LED - 5mm [color="Yellow (585nm)" package="5 mm [THT]"]
  LED5 = LED - 5mm [color="Green (555nm)" package="5 mm [THT]"]
  LED6 = LED - 5mm [color="Green (555nm)" package="5 mm [THT]"]
  R1 = Resistor [tolerance=±5% resistance=220 package=THT]
  R2 = Resistor [tolerance=±5% resistance=220 package=THT]
  R3 = Resistor [tolerance=±5% resistance=220 package=THT]
  R4 = Resistor [tolerance=±5% resistance=220 package=THT]
  R5 = Resistor [tolerance=±5% resistance=220 package=THT]
  R6 = Resistor [tolerance=±5% resistance=220 package=THT]

nets:
  N1: Arduino1.GND, R1.Pin_1, R2.Pin_1, R3.Pin_1, R4.Pin_1, R5.Pin_1, R6.Pin_1
  N2: Arduino1.D7, LED6.cathode
  N3: Arduino1.D6, LED5.cathode
  N4: Arduino1.D5, LED3.cathode
  N5: Arduino1.D4, LED4.cathode
  N6: Arduino1.D3, LED1.cathode
  N7: Arduino1.D2, LED2.cathode
  N8: LED1.anode, R5.Pin_0
  N9: LED2.anode, R6.Pin_0
  N10: LED3.anode, R3.Pin_0
  N11: LED4.anode, R4.Pin_0
  N12: LED5.anode, R2.Pin_0
  N13: LED6.anode, R1.Pin_0
