# Fritzing sketch Bargraph (Advanced) (saved by Fritzing 0.7.0b)
breadboards: 1

parts:
  Arduino2 = Arduino
  LED7 = LED - 5mm [color="Red (635nm)" package="5 mm [THT]"]
  LED8 = LED - 5mm [color="Red (635nm)" package="5 mm [THT]"]
  LED9 = LED - 5mm [color="Yellow (585nm)" package="5 mm [THT]"]
  LED10 = LED - 5mm [color="Yellow (585nm)" package="5 mm [THT]"]
  LED11 = LED - 5mm [color="Green (560nm)" package="5 mm [THT]"]
  LED12 = LED - 5mm [color="Green (560nm)" package="5 mm [THT]"]
  R7 = Resistor [tolerance=±5% resistance=220 package=THT]
  R8 = Resistor [tolerance=±5% resistance=220 package=THT]
  R9 = Resistor [tolerance=±5% resistance=220 package=THT]
  R10 = Resistor [tolerance=±5% resistance=220 package=THT]
  R11 = Resistor [tolerance=±5% resistance=220 package=THT]
  R12 = Resistor [tolerance=±5% resistance=220 package=THT]

nets:
  N1: Arduino2.GND, R7.Pin_1, R8.Pin_1, R9.Pin_1, R10.Pin_1, R11.Pin_1, R12.Pin_1
  N2: Arduino2.D11, LED12.cathode
  N3: Arduino2.D10, LED11.cathode
  N4: Arduino2.D9, LED10.cathode
  N5: Arduino2.D6, LED9.cathode
  N6: Arduino2.D5, LED7.cathode
  N7: Arduino2.D3, LED8.cathode
  N8: LED7.anode, R8.Pin_0
  N9: LED8.anode, R7.Pin_0
  N10: LED9.anode, R9.Pin_0
  N11: LED10.anode, R10.Pin_0
  N12: LED11.anode, R11.Pin_0
  N13: LED12.anode, R12.Pin_0
