# Fritzing sketch Slider (saved by Fritzing 0.7.0b)
breadboards: 1

parts:
  Arduino2 = Arduino
  LED3 = LED - 5mm [color="Red (633nm)" package="5 mm [THT]"]
  R1 = Resistor [tolerance=±5% resistance=220 package=THT]
  R2 = Slide Potentiometer [maximum_resistance=100kΩ]

nets:
  N1: Arduino2.D11, LED3.anode
  N2: Arduino2.+5V, R2.leg1
  N3: Arduino2.GND, R1.Pin_1, R2.leg2
  N4: Arduino2.A0, R2.wiper
  N5: LED3.cathode, R1.Pin_0

// code stored in the sketch: Blink.ino
/*
  Blink
  Turns on an LED on for one second, then off for one second, repeatedly.
 
  This example code is in the public domain.
 */

void setup() {                
  // initialize the digital pin as an output.
  // Pin 13 has an LED connected on most Arduino boards:
  pinMode(13, OUTPUT);     
}

void loop() {
  digitalWrite(13, HIGH);   // set the LED on
  delay(1000);              // wait for a second
  digitalWrite(13, LOW);    // set the LED off
  delay(1000);              // wait for a second
}
