# Fritzing sketch Servo (saved by Fritzing 0.7.0b)
breadboards: 1

parts:
  J1 = Basic Servo
  Arduino3 = Arduino
  LED4 = LED - 5mm [color="Red (633nm)" package="5 mm [THT]"]
  R2 = Resistor [tolerance=±5% resistance=220 package=THT]

nets:
  GND: J1.gnd, Arduino3.GND, R2.Pin_1
  VCC: J1.vcc, Arduino3.+5V
  N1: J1.pulse, Arduino3.D6
  N2: Arduino3.D11, LED4.anode
  N3: LED4.cathode, R2.Pin_0
