# Fritzing sketch Physical Pixel (saved by Fritzing 0.7.0b)
breadboards: 1

parts:
  LED1 = RGB LED - (4 legs) [package="5 mm [THT]"]
  RGB_Shield = Arduino
  R1 = Resistor [tolerance=±5% resistance=220 package=THT]
  R2 = Resistor [tolerance=±5% resistance=220 package=THT]
  R3 = Resistor [tolerance=±5% resistance=220 package=THT]

nets:
  N1: LED1.red_cathode, R1.Pin_0
  N2: LED1.common_anode, RGB_Shield.+5V
  N3: LED1.green_cathode, R2.Pin_0
  N4: LED1.blue_cathode, R3.Pin_0
  N5: RGB_Shield.D11, R1.Pin_1
  N6: RGB_Shield.D10, R2.Pin_1
  N7: RGB_Shield.D9, R3.Pin_1
