# Fritzing sketch Capacitive Sensing (saved by Fritzing 0.7.0b)
breadboards: 1

parts:
  RGB_Shield = Arduino
  R1 = Resistor [tolerance=±5% resistance=1M package=THT]

nets:
  N1: RGB_Shield.D3, R1.Pin_0
  N2: RGB_Shield.D2, R1.Pin_1
